# Fritzing sketch Cardiac Memory [Sidney] (saved by Fritzing 0.9.3b)
breadboards: 1

parts:
  Part1 = Arduino Uno (Rev3) - ICSP
  LED_1 = smd LED [color="White (4500K)" package="1206 [SMD]"]
  LED_2 = smd LED [color="White (4500K)" package="1206 [SMD]"]
  LED_3 = smd LED [color="White (4500K)" package="1206 [SMD]"]
  LED_4 = smd LED [color="White (4500K)" package="1206 [SMD]"]
  R1 = Resistor [tolerance=±5% resistance=220 package="0402 [SMD]"]
  R2 = Resistor [tolerance=±5% resistance=220 package="0402 [SMD]"]
  R3 = Resistor [tolerance=±5% resistance=220 package="0402 [SMD]"]
  R4 = Resistor [tolerance=±5% resistance=220 package="0402 [SMD]"]
  S1 = PHOTOCELL [package=photocell]
  S2 = PHOTOCELL [package=photocell]
  S3 = PHOTOCELL [package=photocell]
  S4 = PHOTOCELL [package=photocell]
  R5 = Resistor [tolerance=±5% resistance=220 package="0402 [SMD]"]
  R6 = Resistor [tolerance=±5% resistance=220 package="0402 [SMD]"]
  R7 = Resistor [tolerance=±5% resistance=220 package="0402 [SMD]"]
  R8 = Resistor [tolerance=±5% resistance=220 package="0402 [SMD]"]
  SP1 = SPEAKER [package=pcb_mount_speaker]
  LED_5 = smd LED [color="Green (555nm)" package="1206 [SMD]"]
  LED_6 = smd LED [color="Red (633nm)" package="1206 [SMD]"]
  R9 = Resistor [tolerance=±5% resistance=220 package="0402 [SMD]"]
  R10 = Resistor [tolerance=±5% resistance=220 package="0402 [SMD]"]

nets:
  N1: Part1.A0, Part1.A1, Part1.A2, Part1.A3, Part1.5V, R5.Pin_0, R6.Pin_0, R7.Pin_0, R8.Pin_0
  N2: Part1.D13/SCK, SP1.-
  N3: Part1.GND, LED_1.cathode, LED_2.cathode, LED_3.cathode, LED_4.cathode, S1.P$1, S2.P$1, S3.P$1, S4.P$1, SP1.+, LED_5.cathode, LED_6.cathode
  N4: Part1.D2, R10.Pin_0
  N5: Part1.D3_PWM, R9.Pin_0
  N6: Part1.D4, R4.Pin_1
  N7: Part1.D5_PWM, R3.Pin_1
  N8: Part1.D6_PWM, R2.Pin_1
  N9: Part1.D7, R1.Pin_1
  N10: LED_1.anode, R1.Pin_0
  N11: LED_2.anode, R2.Pin_0
  N12: LED_3.anode, R3.Pin_0
  N13: LED_4.anode, R4.Pin_0
  N14: S1.P$2, R5.Pin_1
  N15: S2.P$2, R6.Pin_1
  N16: S3.P$2, R7.Pin_1
  N17: S4.P$2, R8.Pin_1
  N18: LED_5.anode, R9.Pin_1
  N19: LED_6.anode, R10.Pin_1
